// Logisim project CPU.circ as structural Verilog: 9 circuits, main circuit MAIN
module ADDER8BIT (
  input  CIN,
  input  in_2,
  input  in_3,
  input  in_4,
  input  in_5,
  input  in_6,
  input  in_7,
  input  in_8,
  input  in_9,
  input  in_10,
  input  in_11,
  input  in_12,
  input  in_13,
  input  in_14,
  input  in_15,
  input  in_16,
  input  in_17,
  output out_18,
  output out_19,
  output out_20,
  output out_21,
  output out_22,
  output out_23,
  output out_24,
  output out_25,
  output COUT
);

  wire adder1bit_2_cout, adder1bit_3_cout, adder1bit_4_cout, adder1bit_5_cout, adder1bit_6_cout,
       adder1bit_7_cout, adder1bit_8_cout;

  ADDER1BIT adder1bit_1 (.A(in_3), .B(in_2), .CIN(adder1bit_2_cout), .COUT(COUT), .SUM(out_18));
  ADDER1BIT adder1bit_2 (.A(in_5), .B(in_4), .CIN(adder1bit_3_cout), .COUT(adder1bit_2_cout), .SUM(out_19));
  ADDER1BIT adder1bit_3 (.A(in_7), .B(in_6), .CIN(adder1bit_4_cout), .COUT(adder1bit_3_cout), .SUM(out_20));
  ADDER1BIT adder1bit_4 (.A(in_9), .B(in_8), .CIN(adder1bit_5_cout), .COUT(adder1bit_4_cout), .SUM(out_21));
  ADDER1BIT adder1bit_5 (.A(in_11), .B(in_10), .CIN(adder1bit_6_cout), .COUT(adder1bit_5_cout), .SUM(out_22));
  ADDER1BIT adder1bit_6 (.A(in_13), .B(in_12), .CIN(adder1bit_7_cout), .COUT(adder1bit_6_cout), .SUM(out_23));
  ADDER1BIT adder1bit_7 (.A(in_15), .B(in_14), .CIN(adder1bit_8_cout), .COUT(adder1bit_7_cout), .SUM(out_24));
  ADDER1BIT adder1bit_8 (.A(in_17), .B(in_16), .CIN(CIN), .COUT(adder1bit_8_cout), .SUM(out_25));
endmodule

module ADDER1BIT (
  input  CIN,
  input  A,
  input  B,
  output SUM,
  output COUT
);

  wire and_1_out, and_2_out, xor_2_out;

  or or_1 (COUT, and_1_out, and_2_out);
  and and_1 (and_1_out, xor_2_out, CIN);
  and and_2 (and_2_out, A, B);
  xor xor_1 (SUM, xor_2_out, CIN);
  xor xor_2 (xor_2_out, A, B);
endmodule

module ALU (
  input  ENABLE,
  input  [1:0] OP,
  input  [7:0] A,
  input  [7:0] B,
  output [7:0] result,
  output SGN
);

  wire and_1_out, and_2_out, and_4_out, not_1_out, not_2_out, not_3_out, not_4_out, or_2_out, or_3_out,
       or_4_out;
  wire [7:0] adder8bit_1_out_25, controlled_buffer_2_out, or_1_out, pull_resistor_1_node,
       pull_resistor_2_node, pull_resistor_3_node, xor_1_out, xor_2_out;
  wire [7:7] and_3_out;

  assign result = ENABLE ? or_1_out : 8'bz;  // Controlled_Buffer controlled_buffer_1
  assign or_1_out = xor_2_out | adder8bit_1_out_25;  // OR_Gate or_1, 8 bits wide
  ADDER8BIT adder8bit_1 (
    .in_16(controlled_buffer_2_out[0]), .in_17(xor_1_out[0]), .CIN(or_3_out),
    .in_2(controlled_buffer_2_out[7]), .in_3(xor_1_out[7]), .in_4(controlled_buffer_2_out[6]),
    .in_5(xor_1_out[6]), .in_6(controlled_buffer_2_out[5]), .in_7(xor_1_out[5]),
    .in_8(controlled_buffer_2_out[4]), .in_9(xor_1_out[4]), .in_10(controlled_buffer_2_out[3]),
    .in_11(xor_1_out[3]), .in_12(controlled_buffer_2_out[2]), .in_13(xor_1_out[2]),
    .in_14(controlled_buffer_2_out[1]), .in_15(xor_1_out[1]), .out_25(adder8bit_1_out_25[0]), .COUT(SGN),
    .out_18(adder8bit_1_out_25[7]), .out_19(adder8bit_1_out_25[6]), .out_20(adder8bit_1_out_25[5]),
    .out_21(adder8bit_1_out_25[4]), .out_22(adder8bit_1_out_25[3]), .out_23(adder8bit_1_out_25[2]),
    .out_24(adder8bit_1_out_25[1]));
  assign controlled_buffer_2_out = or_2_out ? A : 8'bz;  // Controlled_Buffer controlled_buffer_2
  or or_2 (or_2_out, and_3_out[7], and_2_out, and_4_out);
  or or_3 (or_3_out, and_2_out, and_3_out[7]);
  assign xor_1_out = {8{and_3_out[7]}} ^ pull_resistor_1_node;  // XOR_Gate xor_1, 8 bits wide
  Pull_Resistor pull_resistor_1 (.node(pull_resistor_1_node));
  assign pull_resistor_1_node = or_4_out ? B : 8'bz;  // Controlled_Buffer controlled_buffer_3
  or or_4 (or_4_out, and_3_out[7], and_4_out);
  assign xor_2_out = pull_resistor_2_node ^ pull_resistor_3_node;  // XOR_Gate xor_2, 8 bits wide
  Pull_Resistor pull_resistor_2 (.node(pull_resistor_2_node));
  assign pull_resistor_2_node = and_1_out ? B : 8'bz;  // Controlled_Buffer controlled_buffer_4
  and and_1 (and_1_out, OP[0], OP[1]);
  and and_2 (and_2_out, not_1_out, OP[1]);
  and and_3 (and_3_out[7], OP[0], not_2_out);
  and and_4 (and_4_out, not_3_out, not_4_out);
  Pull_Resistor pull_resistor_3 (.node(pull_resistor_3_node));
  assign pull_resistor_3_node = and_1_out ? A : 8'bz;  // Controlled_Buffer controlled_buffer_5
  not not_1 (not_1_out, OP[0]);
  not not_2 (not_2_out, OP[1]);
  not not_3 (not_3_out, OP[0]);
  not not_4 (not_4_out, OP[1]);

  // Notes on the sheet:
  //   8 BIT ALU 4OPCODE
  //   0 -- A + B
  //   1 -- A - B
  //   2 -- A++
  //   3 -- A XOR B
endmodule

module MAIN (
  input  in_1,
  input  in_2,
  input  [2:0] REGADDR,
  input  [1:0] ALUOP,
  input  BUS2ALUB,
  input  ACCENQ,
  input  ACCEQ,
  input  ACCR,
  input  REGR,
  input  ACCSET,
  input  REGSET,
  input  in_12,
  input  REGEQ,
  input  ACC2BUS,
  input  BUS2ACC,
  input  CLK,
  input  RAMSET,
  input  PCENABLE,
  input  RAMEQ,
  output [7:0] out_20,
  output [7:0] out_21,
  output [7:0] out_22
);

  wire controlled_buffer_1_out, controlled_buffer_2_out, controlled_buffer_3_out, controlled_buffer_8_out,
       controlled_buffer_9_out, controlled_buffer_10_out, controlled_buffer_11_out, controlled_buffer_12_out,
       decoder_1_out6, decoder_2_out4, decoder_3_out5;
  wire [7:0] controlled_buffer_5_out, dipswitch_1_sw8, MAR_q, ram_1_dout;

  assign controlled_buffer_1_out = decoder_1_out6 ? REGR : 1'bz;  // Controlled_Buffer controlled_buffer_1
  assign controlled_buffer_2_out = decoder_1_out6 ? REGEQ : 1'bz;  // Controlled_Buffer controlled_buffer_2
  assign controlled_buffer_3_out = decoder_1_out6 ? REGSET : 1'bz;  // Controlled_Buffer controlled_buffer_3
  REG8BIT instructionreg ();  // open: D, ENABLEQ, CLK, R, S, Q
  Decoder #(.select(3)) decoder_1 (
    .out6(decoder_1_out6), .sel(REGADDR));  // open: out0, out1, out2, out3, out4, out5, out7, en
  ALU alu_1 (.OP(ALUOP), .ENABLE(in_2), .A(out_22), .B(controlled_buffer_5_out), .result(out_20));  // open: SGN
  ACC8BIT acc8bit_1 (
    .ENABLEQ(ACCEQ), .D(out_20), .ENABLENOTQ(ACCENQ), .CLK(CLK), .R(ACCR), .S(ACCSET), .Q(out_22),
    .NOTQ(out_22));
  assign out_20 = BUS2ACC ? out_21 : 8'bz;  // Controlled_Buffer controlled_buffer_4
  assign controlled_buffer_5_out = BUS2ALUB ? out_21 : 8'bz;  // Controlled_Buffer controlled_buffer_5
  assign out_21 = ACC2BUS ? out_22 : 8'bz;  // Controlled_Buffer controlled_buffer_6
  PC pc_1 (
    .PCE(PCENABLE), .PCR(controlled_buffer_1_out), .PCEQ(controlled_buffer_2_out), .CLK(CLK), .D(out_21),
    .PCS(controlled_buffer_3_out), .Q(out_21));
  Pull_Resistor pull_resistor_1 (.node(out_21));
  assign out_21 = in_1 ? dipswitch_1_sw8 : 8'bz;  // Controlled_Buffer controlled_buffer_7
  // LedBar #(.inputtype("row")) ledbar_1: pin names not known; wires that end beside it: out_21
  DipSwitch dipswitch_1 (
    .sw1(dipswitch_1_sw8[7]), .sw2(dipswitch_1_sw8[6]), .sw3(dipswitch_1_sw8[5]), .sw4(dipswitch_1_sw8[4]),
    .sw5(dipswitch_1_sw8[3]), .sw6(dipswitch_1_sw8[2]), .sw7(dipswitch_1_sw8[1]), .sw8(dipswitch_1_sw8[0]));
  Decoder #(.select(3)) decoder_2 (
    .out4(decoder_2_out4), .sel(REGADDR));  // open: out0, out1, out2, out3, out5, out6, out7, en
  assign controlled_buffer_8_out = decoder_2_out4 ? REGR : 1'bz;  // Controlled_Buffer controlled_buffer_8
  assign controlled_buffer_9_out = decoder_2_out4 ? REGSET : 1'bz;  // Controlled_Buffer controlled_buffer_9
  Decoder #(.select(3)) decoder_3 (
    .out5(decoder_3_out5), .sel(REGADDR));  // open: out0, out1, out2, out3, out4, out6, out7, en
  assign controlled_buffer_10_out = decoder_3_out5 ? REGEQ : 1'bz;  // Controlled_Buffer controlled_buffer_10
  assign controlled_buffer_11_out = decoder_3_out5 ? REGR : 1'bz;  // Controlled_Buffer controlled_buffer_11
  assign controlled_buffer_12_out = decoder_3_out5 ? REGSET : 1'bz;  // Controlled_Buffer controlled_buffer_12
  REG8BIT MAR (
    .D(out_21), .ENABLEQ(in_12), .CLK(CLK), .R(controlled_buffer_8_out), .S(controlled_buffer_9_out),
    .Q(MAR_q));
  REG8BIT IMMEDIATEREG (
    .D(out_21), .ENABLEQ(controlled_buffer_10_out), .R(controlled_buffer_11_out),
    .S(controlled_buffer_12_out), .Q(out_21));  // open: CLK
  REGFILE regfile_1 (.ADDR(REGADDR), .R(REGR), .S(REGSET), .EQ(REGEQ), .D(out_21), .CLK(CLK), .Q(out_21));
  assign out_21 = RAMEQ ? ram_1_dout : 8'bz;  // Controlled_Buffer controlled_buffer_13
  RAM #(.asyncread("true")) ram_1 (.addr(MAR_q), .we(RAMSET), .oe(RAMEQ), .clk(CLK), .din(out_21), .dout(ram_1_dout));

  // Notes on the sheet:
  //   BUS
  //   ADDR
endmodule

module DLATCH (
  input  D,
  input  CLK,
  input  R,
  output Q,
  output NOTQ
);

  wire nand_1_out, nand_2_out, nand_3_out, nand_4_out, nand_5_out, nand_6_out, not_1_out, not_2_out,
       or_1_out, or_2_out;

  not not_1 (not_1_out, CLK);
  not not_2 (not_2_out, D);
  nand nand_1 (nand_1_out, D, not_1_out);
  or or_1 (or_1_out, R, nand_4_out);
  nand nand_2 (nand_2_out, not_1_out, not_2_out);
  nand nand_3 (nand_3_out, nand_1_out, or_1_out);
  nand nand_4 (nand_4_out, nand_3_out, nand_2_out);
  nand nand_5 (nand_5_out, nand_3_out, CLK);
  nand nand_6 (nand_6_out, CLK, nand_4_out);
  nand nand_7 (Q, nand_5_out, or_2_out);
  or or_2 (or_2_out, R, NOTQ);
  nand nand_8 (NOTQ, Q, nand_6_out);
endmodule

module REG8BIT (
  input  ENABLEQ,
  input  CLK,
  input  R,
  input  S,
  input  [7:0] D,
  output [7:0] Q
);

  wire and_1_out, and_2_out;
  wire [7:0] dlatch_8_q;

  DLATCH dlatch_1 (.CLK(and_2_out), .D(D[7]), .R(and_1_out), .Q(dlatch_8_q[7]));  // open: NOTQ
  DLATCH dlatch_2 (.CLK(and_2_out), .D(D[6]), .R(and_1_out), .Q(dlatch_8_q[6]));  // open: NOTQ
  DLATCH dlatch_3 (.CLK(and_2_out), .D(D[5]), .R(and_1_out), .Q(dlatch_8_q[5]));  // open: NOTQ
  DLATCH dlatch_4 (.CLK(and_2_out), .D(D[4]), .R(and_1_out), .Q(dlatch_8_q[4]));  // open: NOTQ
  DLATCH dlatch_5 (.CLK(and_2_out), .D(D[3]), .R(and_1_out), .Q(dlatch_8_q[3]));  // open: NOTQ
  DLATCH dlatch_6 (.CLK(and_2_out), .D(D[2]), .R(and_1_out), .Q(dlatch_8_q[2]));  // open: NOTQ
  DLATCH dlatch_7 (.CLK(and_2_out), .D(D[1]), .R(and_1_out), .Q(dlatch_8_q[1]));  // open: NOTQ
  DLATCH dlatch_8 (.CLK(and_2_out), .D(D[0]), .R(and_1_out), .Q(dlatch_8_q[0]));  // open: NOTQ
  assign Q = ENABLEQ ? dlatch_8_q : 8'bz;  // Controlled_Buffer controlled_buffer_1
  and and_1 (and_1_out, CLK, R);
  and and_2 (and_2_out, CLK, S);
endmodule

module ACC8BIT (
  input  ENABLENOTQ,
  input  ENABLEQ,
  input  CLK,
  input  R,
  input  S,
  input  [7:0] D,
  output [7:0] NOTQ,
  output [7:0] Q
);

  wire and_1_out, and_2_out;
  wire [7:0] dlatch_8_notq, dlatch_8_q;

  DLATCH dlatch_1 (.CLK(and_2_out), .D(D[7]), .R(and_1_out), .Q(dlatch_8_q[7]), .NOTQ(dlatch_8_notq[7]));
  DLATCH dlatch_2 (.CLK(and_2_out), .D(D[6]), .R(and_1_out), .Q(dlatch_8_q[6]), .NOTQ(dlatch_8_notq[6]));
  DLATCH dlatch_3 (.CLK(and_2_out), .D(D[5]), .R(and_1_out), .Q(dlatch_8_q[5]), .NOTQ(dlatch_8_notq[5]));
  DLATCH dlatch_4 (.CLK(and_2_out), .D(D[4]), .R(and_1_out), .Q(dlatch_8_q[4]), .NOTQ(dlatch_8_notq[4]));
  DLATCH dlatch_5 (.CLK(and_2_out), .D(D[3]), .R(and_1_out), .Q(dlatch_8_q[3]), .NOTQ(dlatch_8_notq[3]));
  DLATCH dlatch_6 (.CLK(and_2_out), .D(D[2]), .R(and_1_out), .Q(dlatch_8_q[2]), .NOTQ(dlatch_8_notq[2]));
  DLATCH dlatch_7 (.CLK(and_2_out), .D(D[1]), .R(and_1_out), .Q(dlatch_8_q[1]), .NOTQ(dlatch_8_notq[1]));
  DLATCH dlatch_8 (.CLK(and_2_out), .D(D[0]), .R(and_1_out), .Q(dlatch_8_q[0]), .NOTQ(dlatch_8_notq[0]));
  assign NOTQ = ENABLENOTQ ? dlatch_8_notq : 8'bz;  // Controlled_Buffer controlled_buffer_1
  assign Q = ENABLEQ ? dlatch_8_q : 8'bz;  // Controlled_Buffer controlled_buffer_2
  and and_1 (and_1_out, CLK, R);
  and and_2 (and_2_out, CLK, S);
endmodule

module REGFILE (
  input  [2:0] ADDR,
  input  R,
  input  S,
  input  EQ,
  input  [7:0] D,
  input  CLK,
  output [7:0] Q
);

  wire controlled_buffer_1_out, controlled_buffer_2_out, controlled_buffer_3_out, controlled_buffer_4_out,
       controlled_buffer_5_out, controlled_buffer_6_out, controlled_buffer_7_out, controlled_buffer_8_out,
       controlled_buffer_9_out, controlled_buffer_10_out, controlled_buffer_11_out, controlled_buffer_12_out,
       decoder_1_out0, decoder_1_out1, decoder_1_out2, decoder_1_out3;

  assign controlled_buffer_1_out = decoder_1_out0 ? R : 1'bz;  // Controlled_Buffer controlled_buffer_1
  assign controlled_buffer_2_out = decoder_1_out0 ? S : 1'bz;  // Controlled_Buffer controlled_buffer_2
  REG8BIT reg8bit_1 (
    .D(D), .ENABLEQ(controlled_buffer_3_out), .CLK(CLK), .R(controlled_buffer_1_out),
    .S(controlled_buffer_2_out), .Q(Q));
  assign controlled_buffer_3_out = decoder_1_out0 ? EQ : 1'bz;  // Controlled_Buffer controlled_buffer_3
  assign controlled_buffer_4_out = decoder_1_out1 ? R : 1'bz;  // Controlled_Buffer controlled_buffer_4
  assign controlled_buffer_5_out = decoder_1_out1 ? EQ : 1'bz;  // Controlled_Buffer controlled_buffer_5
  assign controlled_buffer_6_out = decoder_1_out1 ? S : 1'bz;  // Controlled_Buffer controlled_buffer_6
  REG8BIT reg8bit_2 (
    .D(D), .ENABLEQ(controlled_buffer_5_out), .CLK(CLK), .R(controlled_buffer_4_out),
    .S(controlled_buffer_6_out), .Q(Q));
  assign controlled_buffer_7_out = decoder_1_out2 ? R : 1'bz;  // Controlled_Buffer controlled_buffer_7
  assign controlled_buffer_8_out = decoder_1_out2 ? S : 1'bz;  // Controlled_Buffer controlled_buffer_8
  REG8BIT reg8bit_3 (
    .D(D), .ENABLEQ(controlled_buffer_9_out), .CLK(CLK), .R(controlled_buffer_7_out),
    .S(controlled_buffer_8_out), .Q(Q));
  assign controlled_buffer_9_out = decoder_1_out2 ? EQ : 1'bz;  // Controlled_Buffer controlled_buffer_9
  assign controlled_buffer_10_out = decoder_1_out3 ? R : 1'bz;  // Controlled_Buffer controlled_buffer_10
  assign controlled_buffer_11_out = decoder_1_out3 ? S : 1'bz;  // Controlled_Buffer controlled_buffer_11
  assign controlled_buffer_12_out = decoder_1_out3 ? EQ : 1'bz;  // Controlled_Buffer controlled_buffer_12
  REG8BIT reg8bit_4 (
    .D(D), .ENABLEQ(controlled_buffer_12_out), .CLK(CLK), .R(controlled_buffer_10_out),
    .S(controlled_buffer_11_out), .Q(Q));
  Decoder #(.select(3)) decoder_1 (
    .out0(decoder_1_out0), .out1(decoder_1_out1), .out2(decoder_1_out2), .out3(decoder_1_out3), .sel(ADDR));  // open: out4, out5, out6, out7, en
endmodule

module PC (
  input  PCE,
  input  PCR,
  input  PCEQ,
  input  CLK,
  input  [7:0] D,
  input  PCS,
  output [7:0] Q
);

  wire not_1_out, or_1_out;
  wire [7:0] adder8bit_1_out_25, controlled_buffer_1_out, reg8bit_1_q;

  or or_1 (or_1_out, PCE, PCS);
  assign controlled_buffer_1_out = not_1_out ? adder8bit_1_out_25 : 8'bz;  // Controlled_Buffer controlled_buffer_1
  assign controlled_buffer_1_out = PCS ? D : 8'bz;  // Controlled_Buffer controlled_buffer_2
  not not_1 (not_1_out, PCS);
  REG8BIT reg8bit_1 (.D(controlled_buffer_1_out), .ENABLEQ(1'b1), .CLK(CLK), .R(PCR), .S(or_1_out), .Q(reg8bit_1_q));
  ADDER8BIT adder8bit_1 (
    .in_16(1'b1), .in_17(reg8bit_1_q[0]), .in_3(reg8bit_1_q[7]), .in_5(reg8bit_1_q[6]),
    .in_7(reg8bit_1_q[5]), .in_9(reg8bit_1_q[4]), .in_11(reg8bit_1_q[3]), .in_13(reg8bit_1_q[2]),
    .in_15(reg8bit_1_q[1]), .out_25(adder8bit_1_out_25[0]), .out_18(adder8bit_1_out_25[7]),
    .out_19(adder8bit_1_out_25[6]), .out_20(adder8bit_1_out_25[5]), .out_21(adder8bit_1_out_25[4]),
    .out_22(adder8bit_1_out_25[3]), .out_23(adder8bit_1_out_25[2]), .out_24(adder8bit_1_out_25[1]));  // open: CIN, in_2, in_4, in_6, in_8, in_10, in_12, in_14, COUT
  assign Q = PCEQ ? reg8bit_1_q : 8'bz;  // Controlled_Buffer controlled_buffer_3
endmodule
